// Logisim project work.circ as structural Verilog: 1 circuit, main circuit main
module main (
);

  wire clock_1_out, clock_2_out, comparator_1_lt, not_1_out;
  wire [15:0] buffer_1_out, buffer_2_out, counter_1_q, counter_2_q, multiplexer_1_out, multiplexer_2_out,
       register_1_q, register_2_q, register_3_q, register_4_q;

  Clock clock_1 (.out(clock_1_out));
  Clock clock_2 (.out(clock_2_out));
  Counter #(.width(16), .max('h7)) counter_1 (
    .Q(counter_1_q), .clk(clock_1_out), .clr(1'b0));  // open: load, D, count, carry
  Counter #(.width(16), .max('hfff)) counter_2 (
    .Q(counter_2_q), .clk(clock_2_out), .clr(1'b0));  // open: load, D, count, carry
  Register #(.width(16)) register_1 (.D(register_2_q), .en(1'b1), .Q(register_1_q), .clk(clock_1_out), .clr(1'b0));
  Comparator #(.width(16), .mode("unsigned")) comparator_1 (
    .a(counter_1_q), .b(16'h4), .lt(comparator_1_lt));  // open: gt, eq
  Register #(.width(16)) register_2 (.D(register_3_q), .en(1'b1), .Q(register_2_q), .clk(clock_1_out), .clr(1'b0));
  // Probe on register_1_q
  assign buffer_1_out = register_1_q;  // Buffer buffer_1, 16 bits wide
  // Probe on buffer_1_out
  // Probe on buffer_2_out
  assign buffer_2_out = counter_2_q;  // Buffer buffer_2, 16 bits wide
  // Probe on counter_2_q
  not not_1 (not_1_out, comparator_1_lt);
  Register #(.width(16)) register_3 (.D(register_4_q), .en(1'b1), .Q(register_3_q), .clk(clock_1_out), .clr(1'b0));
  Multiplexer #(.width(16), .enable("false")) multiplexer_1 (
    .in0(register_1_q), .in1(buffer_1_out), .out(multiplexer_1_out), .sel(not_1_out));
  Multiplexer #(.width(16), .enable("false")) multiplexer_2 (
    .in0(buffer_2_out), .in1(counter_2_q), .out(multiplexer_2_out), .sel(comparator_1_lt));
  Register #(.width(16)) register_4 (.D(multiplexer_2_out), .en(1'b1), .Q(register_4_q), .clk(clock_1_out), .clr(1'b0));
  // Probe on multiplexer_1_out
endmodule
